// Logisim project FinalVersionFPA.circ as structural Verilog: 31 circuits, main circuit main
module _1_bit_RS (
  input  [26:0] S,
  input  Enable,
  output [26:0] out_3
);

  wire [26:0] Shifted;
  wire [27:0] bit_extender_1_out, bit_extender_2_out;
  wire [27:27] multiplexer_1_out;

  assign bit_extender_1_out = {{1{1'b0}}, S};  // Bit_Extender bit_extender_1
  assign bit_extender_2_out = {{1{1'b0}}, Shifted};  // Bit_Extender bit_extender_2
  Shifter #(.width(27), .shift("lr")) shifter_1 (.in(S), .\dist (5'b00001), .out(Shifted));
  Multiplexer #(.width(28), .enable("false")) multiplexer_1 (
    .in0(bit_extender_1_out), .in1(bit_extender_2_out), .out({multiplexer_1_out[27], out_3}), .sel(Enable));
endmodule

module main (
  input  [31:0] A,
  input  [31:0] B,
  output Overflow,
  output Underflow,
  output [31:0] A___B,
  output INF,
  output Denormalized,
  output NaN
);

  wire not_1_out, onechecker_1_out_2, zerochecker_1_notzero, zerocheckerexponent_1_out_2,
       zerocheckerfraction_1_out_2;

  ZeroCheckerExponent zerocheckerexponent_1 (.I(A___B[30:22]), .out_2(zerocheckerexponent_1_out_2));
  ZeroCheckerFraction zerocheckerfraction_1 (.I(A___B[21:0]), .out_2(zerocheckerfraction_1_out_2));
  OneChecker onechecker_1 (.in_1(A___B[30:22]), .out_2(onechecker_1_out_2));
  ZeroChecker zerochecker_1 (.A(A___B), .NotZero(zerochecker_1_notzero));
  and and_1 (Denormalized, zerochecker_1_notzero, zerocheckerexponent_1_out_2);
  Floating_Point_Adder floating_point_adder_1 (.A(A), .B(B), .Y(A___B), .Overflow(Overflow), .Underflow(Underflow));
  not not_1 (not_1_out, zerocheckerfraction_1_out_2);
  and and_2 (INF, zerocheckerfraction_1_out_2, onechecker_1_out_2);
  and and_3 (NaN, not_1_out, onechecker_1_out_2);
endmodule

module _2_bit_RS (
  input  [26:0] S,
  input  Enable,
  output [26:0] out_3
);

  wire [26:0] Shifted;
  wire [27:0] bit_extender_1_out, bit_extender_2_out;
  wire [27:27] multiplexer_1_out;

  assign bit_extender_1_out = {{1{1'b0}}, S};  // Bit_Extender bit_extender_1
  assign bit_extender_2_out = {{1{1'b0}}, Shifted};  // Bit_Extender bit_extender_2
  Shifter #(.width(27), .shift("lr")) shifter_1 (.in(S), .\dist (5'b00010), .out(Shifted));
  Multiplexer #(.width(28), .enable("false")) multiplexer_1 (
    .in0(bit_extender_1_out), .in1(bit_extender_2_out), .out({multiplexer_1_out[27], out_3}), .sel(Enable));
endmodule

module _4_bit_RS (
  input  [26:0] S,
  input  Enable,
  output [26:0] out_3
);

  wire [26:0] Shifted;
  wire [27:0] bit_extender_1_out, bit_extender_2_out;
  wire [27:27] multiplexer_1_out;

  assign bit_extender_1_out = {{1{1'b0}}, S};  // Bit_Extender bit_extender_1
  assign bit_extender_2_out = {{1{1'b0}}, Shifted};  // Bit_Extender bit_extender_2
  Shifter #(.width(27), .shift("lr")) shifter_1 (.in(S), .\dist (5'b00100), .out(Shifted));
  Multiplexer #(.width(28), .enable("false")) multiplexer_1 (
    .in0(bit_extender_1_out), .in1(bit_extender_2_out), .out({multiplexer_1_out[27], out_3}), .sel(Enable));
endmodule

module _8_bit_RS (
  input  [26:0] S,
  input  Enable,
  output [26:0] out_3
);

  wire [26:0] Shifted;
  wire [27:0] bit_extender_1_out, bit_extender_2_out;
  wire [27:27] multiplexer_1_out;

  assign bit_extender_1_out = {{1{1'b0}}, S};  // Bit_Extender bit_extender_1
  assign bit_extender_2_out = {{1{1'b0}}, Shifted};  // Bit_Extender bit_extender_2
  Shifter #(.width(27), .shift("lr")) shifter_1 (.in(S), .\dist (5'b01000), .out(Shifted));
  Multiplexer #(.width(28), .enable("false")) multiplexer_1 (
    .in0(bit_extender_1_out), .in1(bit_extender_2_out), .out({multiplexer_1_out[27], out_3}), .sel(Enable));
endmodule

module _16_bit_RS (
  input  [26:0] S,
  input  Enable,
  output [26:0] out_3
);

  wire [26:0] Shifted;
  wire [27:0] bit_extender_1_out, bit_extender_2_out;
  wire [27:27] multiplexer_1_out;

  assign bit_extender_1_out = {{1{1'b0}}, S};  // Bit_Extender bit_extender_1
  assign bit_extender_2_out = {{1{1'b0}}, Shifted};  // Bit_Extender bit_extender_2
  Shifter #(.width(27), .shift("lr")) shifter_1 (.in(S), .\dist (5'b10000), .out(Shifted));
  Multiplexer #(.width(28), .enable("false")) multiplexer_1 (
    .in0(bit_extender_1_out), .in1(bit_extender_2_out), .out({multiplexer_1_out[27], out_3}), .sel(Enable));
endmodule

module Right_Shifter (
  input  [4:0] E,
  input  [26:0] A,
  output [26:0] Y
);

  wire [26:0] n2_bit_rs_1_out_3, n4_bit_rs_1_out_3, n8_bit_rs_1_out_3, n16_bit_rs_1_out_3;

  _16_bit_RS u_16_bit_rs_1 (.S(A), .out_3(n16_bit_rs_1_out_3), .Enable(E[4]));
  _8_bit_RS u_8_bit_rs_1 (.S(n16_bit_rs_1_out_3), .out_3(n8_bit_rs_1_out_3), .Enable(E[3]));
  _4_bit_RS u_4_bit_rs_1 (.S(n8_bit_rs_1_out_3), .out_3(n4_bit_rs_1_out_3), .Enable(E[2]));
  _2_bit_RS u_2_bit_rs_1 (.S(n4_bit_rs_1_out_3), .out_3(n2_bit_rs_1_out_3), .Enable(E[1]));
  _1_bit_RS u_1_bit_rs_1 (.Enable(E[0]), .S(n2_bit_rs_1_out_3), .out_3(Y));
endmodule

module Re_arranger (
  input  [8:0] P,
  input  [8:0] Q,
  input  [31:0] A,
  input  [31:0] B,
  output [31:0] larger,
  output [31:0] smaller
);

  wire b_t;

  // Probe on A
  // Probe on B
  // Probe on P
  // Probe on Q
  Subtractor #(.width(9)) subtractor_1 (.a(P), .b(Q), .bin(1'b0), .bout(b_t));  // open: out
  Multiplexer #(.width(32), .enable("false")) multiplexer_1 (.in0(A), .in1(B), .out(larger), .sel(b_t));
  // Probe on larger
  Multiplexer #(.width(32), .enable("false")) multiplexer_2 (.in0(B), .in1(A), .out(smaller), .sel(b_t));
  // Probe on smaller
endmodule

module _1_bit_LS (
  input  [26:0] S,
  input  Enable,
  output [26:0] out_3
);

  wire [26:0] Shifted;
  wire [27:0] bit_extender_1_out, bit_extender_2_out;
  wire [27:27] multiplexer_1_out;

  assign bit_extender_1_out = {{1{1'b0}}, S};  // Bit_Extender bit_extender_1
  assign bit_extender_2_out = {{1{1'b0}}, Shifted};  // Bit_Extender bit_extender_2
  Shifter #(.width(27)) shifter_1 (.in(S), .\dist (5'b00001), .out(Shifted));
  Multiplexer #(.width(28), .enable("false")) multiplexer_1 (
    .in0(bit_extender_1_out), .in1(bit_extender_2_out), .out({multiplexer_1_out[27], out_3}), .sel(Enable));
endmodule

module _2_bit_LS (
  input  [26:0] S,
  input  Enable,
  output [26:0] out_3
);

  wire [26:0] Shifted;
  wire [27:0] bit_extender_1_out, bit_extender_2_out;
  wire [27:27] multiplexer_1_out;

  assign bit_extender_1_out = {{1{1'b0}}, S};  // Bit_Extender bit_extender_1
  assign bit_extender_2_out = {{1{1'b0}}, Shifted};  // Bit_Extender bit_extender_2
  Shifter #(.width(27)) shifter_1 (.in(S), .\dist (5'b00010), .out(Shifted));
  Multiplexer #(.width(28), .enable("false")) multiplexer_1 (
    .in0(bit_extender_1_out), .in1(bit_extender_2_out), .out({multiplexer_1_out[27], out_3}), .sel(Enable));
endmodule

module _4_bit_LS (
  input  [26:0] S,
  input  Enable,
  output [26:0] out_3
);

  wire [26:0] Shifted;
  wire [27:0] bit_extender_1_out, bit_extender_2_out;
  wire [27:27] multiplexer_1_out;

  assign bit_extender_1_out = {{1{1'b0}}, S};  // Bit_Extender bit_extender_1
  assign bit_extender_2_out = {{1{1'b0}}, Shifted};  // Bit_Extender bit_extender_2
  Shifter #(.width(27)) shifter_1 (.in(S), .\dist (5'b00100), .out(Shifted));
  Multiplexer #(.width(28), .enable("false")) multiplexer_1 (
    .in0(bit_extender_1_out), .in1(bit_extender_2_out), .out({multiplexer_1_out[27], out_3}), .sel(Enable));
endmodule

module _8_bit_LS (
  input  [26:0] S,
  input  Enable,
  output [26:0] out_3
);

  wire [26:0] Shifted;
  wire [27:0] bit_extender_1_out, bit_extender_2_out;
  wire [27:27] multiplexer_1_out;

  assign bit_extender_1_out = {{1{1'b0}}, S};  // Bit_Extender bit_extender_1
  assign bit_extender_2_out = {{1{1'b0}}, Shifted};  // Bit_Extender bit_extender_2
  Shifter #(.width(27)) shifter_1 (.in(S), .\dist (5'b01000), .out(Shifted));
  Multiplexer #(.width(28), .enable("false")) multiplexer_1 (
    .in0(bit_extender_1_out), .in1(bit_extender_2_out), .out({multiplexer_1_out[27], out_3}), .sel(Enable));
endmodule

module _16_bit_LS (
  input  [26:0] S,
  input  Enable,
  output [26:0] out_3
);

  wire [26:0] Shifted;
  wire [27:0] bit_extender_1_out, bit_extender_2_out;
  wire [27:27] multiplexer_1_out;

  assign bit_extender_1_out = {{1{1'b0}}, S};  // Bit_Extender bit_extender_1
  assign bit_extender_2_out = {{1{1'b0}}, Shifted};  // Bit_Extender bit_extender_2
  Shifter #(.width(27)) shifter_1 (.in(S), .\dist (5'b10000), .out(Shifted));
  Multiplexer #(.width(28), .enable("false")) multiplexer_1 (
    .in0(bit_extender_1_out), .in1(bit_extender_2_out), .out({multiplexer_1_out[27], out_3}), .sel(Enable));
endmodule

module Right_Shifter_Adapter (
  input  [8:0] S,
  output [4:0] E
);

  wire n7432_1_p2;

  // Probe on S
  // _7432 7432_1: pin names not known; wires that end beside it: S[4], n7432_1_p2, E[4], S[3], n7432_1_p2, E[3], n7432_1_p2, S[1], E[1], n7432_1_p2, S[2], E[2]
  Subtractor #(.width(9)) subtractor_1 (.a(9'h1a), .b(S), .bin(1'b0), .bout(n7432_1_p2));  // open: out
  // _7432 7432_2: pin names not known; wires that end beside it: S[0], n7432_1_p2, E[0], n7432_1_p2, n7432_1_p2, n7432_1_p2
endmodule

module Left_Shifter (
  input  [4:0] E,
  input  [26:0] A,
  output [26:0] Y
);

  wire [26:0] n2_bit_ls_1_out_3, n4_bit_ls_1_out_3, n8_bit_ls_1_out_3, n16_bit_ls_1_out_3;

  // Probe on A
  _16_bit_LS u_16_bit_ls_1 (.S(A), .out_3(n16_bit_ls_1_out_3), .Enable(E[4]));
  _8_bit_LS u_8_bit_ls_1 (.S(n16_bit_ls_1_out_3), .out_3(n8_bit_ls_1_out_3), .Enable(E[3]));
  _4_bit_LS u_4_bit_ls_1 (.S(n8_bit_ls_1_out_3), .out_3(n4_bit_ls_1_out_3), .Enable(E[2]));
  _2_bit_LS u_2_bit_ls_1 (.S(n4_bit_ls_1_out_3), .out_3(n2_bit_ls_1_out_3), .Enable(E[1]));
  // Probe on Y
  _1_bit_LS u_1_bit_ls_1 (.S(n2_bit_ls_1_out_3), .out_3(Y), .Enable(E[0]));
endmodule

module Right_Shift_Wrapper (
  input  [25:0] A,
  input  [8:0] S,
  output [25:0] Y
);

  wire [4:0] right_shifter_adapter_1_e;
  wire [26:0] bit_extender_1_out;
  wire [26:26] right_shifter_1_y;

  assign bit_extender_1_out = {{1{1'b0}}, A};  // Bit_Extender bit_extender_1
  // Probe on S
  // Probe on bit_extender_1_out
  Right_Shifter_Adapter right_shifter_adapter_1 (.S(S), .E(right_shifter_adapter_1_e));
  Right_Shifter right_shifter_1 (.A(bit_extender_1_out), .E(right_shifter_adapter_1_e), .Y({right_shifter_1_y[26], Y}));
  // Probe on Y
endmodule

module Rounder (
  input  [24:0] S,
  input  [8:0] Exponent,
  output [21:0] R,
  output [8:0] RoundedExponent,
  output RoundingOverflow
);

  wire adder_1_cout, adder_2_cout, n7408_1_p3, n7432_1_p3, n7432_1_p6;
  wire [8:0] bit_extender_2_out;
  wire [21:0] bit_extender_1_out;

  // _7432 7432_1: pin names not known; wires that end beside it: S[1], S[0], n7432_1_p3, S[3], n7432_1_p3, n7432_1_p6
  Adder #(.width(22)) adder_1 (.a(S[24:3]), .b(bit_extender_1_out), .out(R), .cin(n7408_1_p3), .cout(adder_1_cout));
  assign bit_extender_1_out = {{21{1'b0}}, 1'b0};  // Bit_Extender bit_extender_1
  // _7408 7408_1: pin names not known; wires that end beside it: S[2], n7432_1_p6, n7408_1_p3
  assign bit_extender_2_out = {{8{1'b0}}, 1'b0};  // Bit_Extender bit_extender_2
  Adder #(.width(9)) adder_2 (
    .a(Exponent), .b(bit_extender_2_out), .out(RoundedExponent), .cin(adder_1_cout), .cout(adder_2_cout));
  Error_detector error_detector_1 (
    .Carry_borrow(adder_2_cout), .Exponent(RoundedExponent), .Overflow_Underflow(RoundingOverflow));

  // Other names for the same wires on the sheet: Sticky = S[0]; Round = S[1]; Guard = S[2]; S0 = S[3];
  //   S_t[21:0] = S[24:3]
endmodule

module _74148 (
  input  _1__I4,
  input  _16__Vcc,
  input  _2__I5,
  input  _3__I6,
  input  _4__I7,
  input  _13__I3,
  input  _5__EI,
  input  _12__I2,
  input  _11__I1,
  input  _10__I0,
  input  _8__GND,
  output _15__EO,
  output _16__GS,
  output _6__A2,
  output _7__A1,
  output _9__A0
);

  wire not_1_out, not_2_out, not_3_out, not_4_out, not_5_out, not_6_out, not_7_out, not_8_out, not_9_out,
       not_10_out, not_11_out, not_12_out, priority_encoder_1_en_out, priority_encoder_1_gs;
  wire [2:0] priority_encoder_1_out;

  or or_1 (_16__GS, priority_encoder_1_en_out, _5__EI);
  not not_1 (not_1_out, _10__I0);
  not not_2 (not_2_out, _11__I1);
  not not_3 (not_3_out, _12__I2);
  Priority_Encoder #(.disabled(0)) priority_encoder_1 (
    .in0(not_1_out), .in1(not_2_out), .in2(not_3_out), .in3(not_4_out), .in4(not_5_out), .in5(not_6_out),
    .in6(not_7_out), .in7(not_8_out), .out(priority_encoder_1_out), .en_in(not_9_out),
    .gs(priority_encoder_1_gs), .en_out(priority_encoder_1_en_out));
  not not_4 (not_4_out, _13__I3);
  not not_5 (not_5_out, _1__I4);
  not not_6 (not_6_out, _2__I5);
  not not_7 (not_7_out, _3__I6);
  not not_8 (not_8_out, _4__I7);
  not not_9 (not_9_out, _5__EI);
  or or_2 (_15__EO, priority_encoder_1_gs, _5__EI);
  not not_10 (not_10_out, priority_encoder_1_out[0]);
  not not_11 (not_11_out, priority_encoder_1_out[1]);
  not not_12 (not_12_out, priority_encoder_1_out[2]);
  or or_3 (_9__A0, not_10_out, _16__GS);
  or or_4 (_7__A1, not_11_out, _16__GS);
  or or_5 (_6__A2, not_12_out, _16__GS);

  // Other names for the same wires on the sheet: A0 = _9__A0; A1 = _7__A1; A2 = _6__A2; E = _5__EI; EO = _15__EO;
  //   GS = _16__GS; I0 = _10__I0; I1 = _11__I1; I2 = _12__I2; I3 = _13__I3; I4 = _1__I4; I5 = _2__I5; I6 = _3__I6;
  //   I7 = _4__I7

  // Notes on the sheet:
  //   _8__GND: pull=down
  //   _16__Vcc: pull=up
  //   74148: 8-Line to 4-Line Priority Encoder
endmodule

module Error_detector (
  input  [8:0] Exponent,
  input  Carry_borrow,
  output Overflow_Underflow
);

  Subtractor #(.width(10)) subtractor_1 (
    .a(10'h1fe), .b({Carry_borrow, Exponent}), .bout(Overflow_Underflow));  // open: out, bin
endmodule

module Normalizer (
  input  [26:0] Significand,
  input  [8:0] Exponent,
  output [24:0] Normal_Significand,
  output [8:0] Normal_Exponent,
  output Normalizing_Overflow,
  output Underflow
);

  wire Add, Carry, E0, E1, E2, E3, E4, E8, n7402_1_p1, n7432_2_p3, n7432_2_p6, n7432_2_p8, n7432_2_p9,
       n7432_3_p3, n7432_3_p6, Overflow_underflow, Sub;
  wire [4:0] bit_extender_1_out, LeftShiftAmount, multiplexer_1_out;
  wire [5:5] n32_bit_input_high_encoder_1_o;
  wire [8:0] ModifiedExponent;
  wire [26:0] bit_extender_2_out, bit_extender_3_out, n1_bit_rs_1_out_3;
  wire [26:25] left_shifter_1_y;
  wire [27:10] asu_1_y;

  // _7432 7432_1: pin names not known; wires that end beside it: Significand[25], Significand[26], Add
  // _7404 7404_1: pin names not known; wires that end beside it: Add, Sub
  // _7432 7432_2: pin names not known; wires that end beside it: Significand[26], LeftShiftAmount[0], n7432_2_p3, n7432_2_p3, LeftShiftAmount[1], n7432_2_p6, LeftShiftAmount[2], n7432_2_p8, n7432_2_p9, LeftShiftAmount[3], n7432_2_p6, n7432_2_p8
  _1_bit_RS u_1_bit_rs_1 (.Enable(Significand[26]), .S(Significand), .out_3(n1_bit_rs_1_out_3));
  assign bit_extender_1_out = {{4{1'b0}}, Significand[26]};  // Bit_Extender bit_extender_1
  _32_bit_input_high_encoder u_32_bit_input_high_encoder_1 (
    .I({Significand[24:0], {7{1'b0}}}), ._1_based_indexing(1'b1),
    .O({n32_bit_input_high_encoder_1_o[5], LeftShiftAmount}));
  Left_Shifter left_shifter_1 (
    .A(n1_bit_rs_1_out_3), .E({E4, E3, E2, E1, E0}), .Y({left_shifter_1_y, Normal_Significand}));
  Multiplexer #(.width(5), .enable("false")) multiplexer_1 (
    .in0(LeftShiftAmount), .in1(bit_extender_1_out), .out(multiplexer_1_out), .sel(Add));
  // _7432 7432_3: pin names not known; wires that end beside it: LeftShiftAmount[4], n7432_2_p9, n7432_3_p3, n7432_3_p3, Significand[25], n7432_3_p6, Exponent
  // _7408 7408_1: pin names not known; wires that end beside it: n7432_3_p6, E8, Carry, Add, Overflow_underflow, Normalizing_Overflow, Overflow_underflow, Sub, Underflow
  assign bit_extender_2_out = {{22{1'b0}}, multiplexer_1_out};  // Bit_Extender bit_extender_2
  assign bit_extender_3_out = {{18{1'b0}}, Exponent};  // Bit_Extender bit_extender_3
  // _7402 7402_1: pin names not known; wires that end beside it: n7402_1_p1, Significand[25], Significand[26]
  ASU asu_1 (
    .B_Cin(1'b0), .A(bit_extender_3_out), .B(bit_extender_2_out), .Y({asu_1_y, E8, ModifiedExponent}),
    .Add(Add));
  Multiplexer #(.width(9), .enable("false")) multiplexer_2 (
    .in0({9{1'b0}}), .in1(ModifiedExponent), .out(Normal_Exponent), .sel(n7432_3_p6));
  // _7408 7408_2: pin names not known; wires that end beside it: n7402_1_p1, LeftShiftAmount[4], E4, n7402_1_p1, LeftShiftAmount[3], E3, n7402_1_p1, LeftShiftAmount[2], E2, n7402_1_p1, LeftShiftAmount[1], E1
  Error_detector error_detector_1 (
    .Carry_borrow(Carry), .Exponent(Normal_Exponent), .Overflow_Underflow(Overflow_underflow));
  // _7408 7408_3: pin names not known; wires that end beside it: n7402_1_p1, LeftShiftAmount[0], E0

  // Other names for the same wires on the sheet: O0 = LeftShiftAmount[0]; O1 = LeftShiftAmount[1];
  //   O2 = LeftShiftAmount[2]; O3 = LeftShiftAmount[3]; O4 = LeftShiftAmount[4]; Overflow = Normalizing_Overflow;
  //   S26 = Significand[25]; S27 = Significand[26]
endmodule

module Floating_Point_Adder (
  input  [31:0] A,
  input  [31:0] B,
  output [31:0] Y,
  output Overflow,
  output Underflow
);

  wire A_pre_decimal, B_pre_decimal, n7404_1_p1, NormalizationOverflow, RoundingOverflow, SameSign;
  wire [8:0] exponent_difference, larger_exponent, NormalExponent, smaller_exponent;
  wire [24:0] NormalSignificand;
  wire [24:3] padded_significand_2_prime;
  wire [25:0] multiplexer_1_out, multiplexer_2_out, padded_significand_2;
  wire [26:0] AddedSignificand, ASUInput1, ASUInput2;
  wire [27:0] ASUOutput;
  wire [31:0] larger_exponent_float;
  wire [31:31] smaller_exponent_float;

  Subtractor #(.width(9)) subtractor_1 (
    .a(larger_exponent), .b(smaller_exponent), .out(exponent_difference), .bin(1'b0));  // open: bout
  Right_Shift_Wrapper right_shift_wrapper_1 (
    .A({B_pre_decimal, padded_significand_2_prime, 3'b000}), .S(exponent_difference), .Y(padded_significand_2));
  // _7404 7404_1: pin names not known; wires that end beside it: n7404_1_p1, SameSign
  // _7486 7486_1: pin names not known; wires that end beside it: A[31], B[31], n7404_1_p1
  ZeroChecker zerochecker_1 (
    .A({larger_exponent_float[31], larger_exponent, larger_exponent_float[21:0]}), .NotZero(A_pre_decimal));
  Normalizer normalizer_1 (
    .Significand(AddedSignificand), .Exponent(larger_exponent), .Normal_Significand(NormalSignificand),
    .Normal_Exponent(NormalExponent), .Underflow(Underflow), .Normalizing_Overflow(NormalizationOverflow));
  Rounder rounder_1 (
    .S(NormalSignificand), .R(Y[21:0]), .Exponent(NormalExponent), .RoundedExponent(Y[30:22]),
    .RoundingOverflow(RoundingOverflow));
  Re_arranger re_arranger_1 (
    .P(A[30:22]), .Q(B[30:22]), .A(A), .B(B),
    .larger({larger_exponent_float[31], larger_exponent, larger_exponent_float[21:0]}),
    .smaller({smaller_exponent_float[31], smaller_exponent, padded_significand_2_prime}));
  ABS abs_1 (.A(ASUOutput), .ABS(AddedSignificand));
  ASU asu_1 (.B_Cin(1'b0), .A(ASUInput1), .B(ASUInput2), .Y(ASUOutput), .Add(SameSign));
  ZeroChecker zerochecker_2 (
    .A({smaller_exponent_float[31], smaller_exponent, padded_significand_2_prime}), .NotZero(B_pre_decimal));
  Multiplexer #(.width(26), .enable("false")) multiplexer_1 (
    .in0({A_pre_decimal, larger_exponent_float[21:0], 3'b000}), .in1(padded_significand_2),
    .out(multiplexer_1_out), .sel(larger_exponent_float[31]));
  Multiplexer #(.width(26), .enable("false")) multiplexer_2 (
    .in0(padded_significand_2), .in1({A_pre_decimal, larger_exponent_float[21:0], 3'b000}),
    .out(multiplexer_2_out), .sel(larger_exponent_float[31]));
  // _7432 7432_1: pin names not known; wires that end beside it: NormalizationOverflow, RoundingOverflow, Overflow
  // _74157 74157_1: pin names not known; wires that end beside it: SameSign, ASUOutput[26], A[31], Y[31], 1'b0
  assign ASUInput1 = {{1{1'b0}}, multiplexer_1_out};  // Bit_Extender bit_extender_1
  assign ASUInput2 = {{1{1'b0}}, multiplexer_2_out};  // Bit_Extender bit_extender_2

  // Other names for the same wires on the sheet: Significand_A[21:0] = A[21:0]; Exponent_A[8:0] = A[30:22];
  //   Sign_A = A[31]; SumSign = ASUOutput[26]; Significand_B[21:0] = B[21:0]; Exponent_B[8:0] = B[30:22];
  //   Sign_B = B[31]; larger_exponent_float[30:22] = larger_exponent; RearrangedSign1 = larger_exponent_float[31];
  //   padded_significand_1[25:3] = {A_pre_decimal, larger_exponent_float[21:0]};
  //   significand_of_larger_exp[21:0] = larger_exponent_float[21:0];
  //   significand_of_smaller_exp[21:0] = padded_significand_2_prime;
  //   smaller_exponent_float[30:0] = {smaller_exponent, padded_significand_2_prime};
  //   padded_significand_2_prime[25] = B_pre_decimal; RoundedSignificand[21:0] = Y[21:0];
  //   RoundedExponent[8:0] = Y[30:22]; Sign = Y[31]
endmodule

module ZeroChecker (
  input  [31:0] A,
  output NotZero
);

  wire n7432_1_p3, n7432_1_p6, n7432_1_p8, n7432_1_p9, n7432_2_p3, n7432_2_p6, n7432_2_p8, n7432_2_p9,
       n7432_3_p3, n7432_3_p6, n7432_3_p8, n7432_3_p9, n7432_4_p3, n7432_4_p6, n7432_4_p8, n7432_4_p9,
       n7432_5_p3, n7432_5_p6, n7432_5_p8, n7432_5_p9, n7432_6_p3, n7432_6_p6, n7432_6_p8, n7432_6_p9,
       n7432_7_p3, n7432_7_p6, n7432_7_p8, n7432_7_p9, n7432_8_p3, n7432_8_p7;

  // _7432 7432_1: pin names not known; wires that end beside it: A[0], A[1], n7432_1_p3, n7432_1_p3, A[2], n7432_1_p6, A[3], n7432_1_p8, n7432_1_p9, A[4], n7432_1_p6, n7432_1_p8
  // _7432 7432_2: pin names not known; wires that end beside it: n7432_1_p9, A[5], n7432_2_p3, n7432_2_p3, A[6], n7432_2_p6, A[7], n7432_2_p8, n7432_2_p9, A[8], n7432_2_p6, n7432_2_p8
  // _7432 7432_3: pin names not known; wires that end beside it: n7432_2_p9, A[9], n7432_3_p3, n7432_3_p3, A[10], n7432_3_p6, A[11], n7432_3_p8, n7432_3_p9, A[12], n7432_3_p6, n7432_3_p8
  // _7432 7432_4: pin names not known; wires that end beside it: n7432_3_p9, A[13], n7432_4_p3, n7432_4_p3, A[14], n7432_4_p6, A[15], n7432_4_p8, n7432_4_p9, A[16], n7432_4_p6, n7432_4_p8
  // _7432 7432_5: pin names not known; wires that end beside it: n7432_4_p9, A[17], n7432_5_p3, n7432_5_p3, A[18], n7432_5_p6, A[19], n7432_5_p8, n7432_5_p9, A[20], n7432_5_p6, n7432_5_p8
  // _7432 7432_6: pin names not known; wires that end beside it: n7432_5_p9, A[21], n7432_6_p3, n7432_6_p3, A[22], n7432_6_p6, A[23], n7432_6_p8, n7432_6_p9, A[24], n7432_6_p6, n7432_6_p8
  // _7432 7432_7: pin names not known; wires that end beside it: n7432_6_p9, A[25], n7432_7_p3, n7432_7_p3, A[26], n7432_7_p6, A[27], n7432_7_p8, n7432_7_p9, A[28], n7432_7_p6, n7432_7_p8
  // _7432 7432_8: pin names not known; wires that end beside it: n7432_7_p9, A[29], n7432_8_p3, n7432_8_p3, A[30], NotZero, n7432_8_p7, A[31], n7432_8_p7
endmodule

module _16_bit_priority_encoder (
  input  [15:0] I,
  input  EI,
  output [3:0] O,
  output EO,
  output GS
);

  wire A0_0, A0_1, A1_0, A1_1, A2_0, A2_1, GS_0, n74148_1__15__eo;

  _74148 u_74148_1 (
    ._1__I4(I[12]), ._2__I5(I[13]), ._3__I6(I[14]), ._4__I7(I[15]), ._5__EI(EI), ._6__A2(A2_1),
    ._7__A1(A1_1), ._15__EO(n74148_1__15__eo), ._16__GS(O[3]), ._13__I3(I[11]), ._12__I2(I[10]),
    ._11__I1(I[9]), ._10__I0(I[8]), ._9__A0(A0_1));  // open: _8__GND, _16__Vcc
  _74148 u_74148_2 (
    ._1__I4(I[4]), ._2__I5(I[5]), ._3__I6(I[6]), ._4__I7(I[7]), ._5__EI(n74148_1__15__eo), ._6__A2(A2_0),
    ._7__A1(A1_0), ._15__EO(EO), ._16__GS(GS_0), ._13__I3(I[3]), ._12__I2(I[2]), ._11__I1(I[1]),
    ._10__I0(I[0]), ._9__A0(A0_0));  // open: _8__GND, _16__Vcc
  // _7408 7408_1: pin names not known; wires that end beside it: A2_1, A2_0, O[2], A1_1, A1_0, O[1], A0_1, A0_0, O[0], GS_0, O[3], GS

  // Other names for the same wires on the sheet: A0 = O[0]; A1 = O[1]; A2 = O[2]; A3 = O[3]
endmodule

module _32_bit_encoder (
  input  EI,
  input  [31:0] I,
  output [4:0] O
);

  wire n16_bit_priority_encoder_1_eo, O0_0, O0_1, O1_0, O1_1, O2_0, O2_1, O3_0, O3_1;

  _16_bit_priority_encoder u_16_bit_priority_encoder_1 (
    .EI(EI), .EO(n16_bit_priority_encoder_1_eo), .GS(O[4]), .I(I[31:16]), .O({O3_1, O2_1, O1_1, O0_1}));
  _16_bit_priority_encoder u_16_bit_priority_encoder_2 (
    .EI(n16_bit_priority_encoder_1_eo), .I(I[15:0]), .O({O3_0, O2_0, O1_0, O0_0}));  // open: EO, GS
  // _7408 7408_1: pin names not known; wires that end beside it: O2_1, O2_0, O[2], O1_1, O1_0, O[1], O0_1, O0_0, O[0], O3_1, O3_0, O[3]

  // Other names for the same wires on the sheet: I0[15:0] = I[15:0]; I1[15:0] = I[31:16];
  //   O_0[3:0] = {O3_0, O2_0, O1_0, O0_0}; O_1[3:0] = {O3_1, O2_1, O1_1, O0_1}
endmodule

module _32_bit_input_high_encoder (
  input  [31:0] I,
  input  _1_based_indexing,
  output [5:0] O
);

  wire I0_prime, I1_prime, I2_prime, I3_prime, I4_prime, I5_prime, I6_prime, I7_prime, I8_prime, I9_prime,
       I10_prime, I11_prime, I12_prime, I13_prime, I14_prime, I15_prime, I16_prime, I17_prime, I18_prime,
       I19_prime, I20_prime, I21_prime, I22_prime, I23_prime, I24_prime, I25_prime, I26_prime, I27_prime,
       I28_prime, I29_prime, I30_prime, I31_prime;
  wire [4:0] bit_extender_1_out, n32_bit_encoder_1_o;

  // _7404 7404_1: pin names not known; wires that end beside it: I[0], I0_prime, I[1], I1_prime, I[2], I2_prime, I[3], I3_prime, I[4], I4_prime, I[5], I5_prime
  // _7404 7404_2: pin names not known; wires that end beside it: I[6], I6_prime, I[7], I7_prime, I[8], I8_prime, I[9], I9_prime, I[10], I10_prime, I[11], I11_prime
  // _7404 7404_3: pin names not known; wires that end beside it: I[12], I12_prime, I[13], I13_prime, I[14], I14_prime, I[15], I15_prime, I[16], I16_prime, I[17], I17_prime
  // _7404 7404_4: pin names not known; wires that end beside it: I[18], I18_prime, I[19], I19_prime, I[20], I20_prime, I[21], I21_prime, I[22], I22_prime, I[23], I23_prime
  // _7404 7404_5: pin names not known; wires that end beside it: I[24], I24_prime, I[25], I25_prime, I[26], I26_prime, I[27], I27_prime, I[28], I28_prime, I[29], I29_prime
  // _7404 7404_6: pin names not known; wires that end beside it: I[30], I30_prime, I[31], I31_prime
  _32_bit_encoder u_32_bit_encoder_1 (
    .EI(1'b0),
    .I({I31_prime, I30_prime, I29_prime, I28_prime, I27_prime, I26_prime, I25_prime, I24_prime, I23_prime, I22_prime, I21_prime, I20_prime, I19_prime, I18_prime, I17_prime, I16_prime, I15_prime, I14_prime, I13_prime, I12_prime, I11_prime, I10_prime, I9_prime, I8_prime, I7_prime, I6_prime, I5_prime, I4_prime, I3_prime, I2_prime, I1_prime, I0_prime}),
    .O(n32_bit_encoder_1_o));
  assign bit_extender_1_out = {{4{1'b0}}, 1'b0};  // Bit_Extender bit_extender_1
  Adder #(.width(5)) adder_1 (
    .a(n32_bit_encoder_1_o), .b(bit_extender_1_out), .out(O[4:0]), .cin(_1_based_indexing), .cout(O[5]));

  // Other names for the same wires on the sheet: I_prime[31:0] = {I31_prime, I30_prime, I29_prime, I28_prime, I27_prime, I26_prime, I25_prime, I24_prime, I23_prime, I22_prime, I21_prime, I20_prime, I19_prime, I18_prime, I17_prime, I16_prime, I15_prime, I14_prime, I13_prime, I12_prime, I11_prime, I10_prime, I9_prime, I8_prime, I7_prime, I6_prime, I5_prime, I4_prime, I3_prime, I2_prime, I1_prime, I0_prime}
endmodule

module ASU (
  input  B_Cin,
  input  Add,
  input  [26:0] A,
  input  [26:0] B,
  output [27:0] Y
);

  wire bout, cout;
  wire [26:0] Add_t, Sub;

  // Probe on B
  // Probe on A
  Adder #(.width(27)) adder_1 (.a(A), .b(B), .out(Add_t), .cin(B_Cin), .cout(cout));
  Subtractor #(.width(27)) subtractor_1 (.a(A), .b(B), .out(Sub), .bin(B_Cin), .bout(bout));
  // _74157 74157_1: pin names not known; wires that end beside it: Add, bout, cout, Y[27], 1'b0
  Multiplexer #(.width(27), .enable("false")) multiplexer_1 (.in0(Sub), .in1(Add_t), .out(Y[26:0]), .sel(Add));
  // Probe on Y
endmodule

module ABS (
  input  [27:0] A,
  output [26:0] ABS
);

  wire [26:0] _1_s_Comp, bit_extender_1_out;

  // _7486 7486_1: pin names not known; wires that end beside it: A[0], A[27], _1_s_Comp[0], A[1], A[27], _1_s_Comp[1], A[27], A[3], _1_s_Comp[3], A[27], A[2], _1_s_Comp[2]
  // _7486 7486_2: pin names not known; wires that end beside it: A[16], A[27], _1_s_Comp[16], A[17], A[27], _1_s_Comp[17], A[27], A[19], _1_s_Comp[19], A[27], A[18], _1_s_Comp[18]
  // Probe on A
  // _7486 7486_3: pin names not known; wires that end beside it: A[4], A[27], _1_s_Comp[4], A[5], A[27], _1_s_Comp[5], A[27], A[7], _1_s_Comp[7], A[27], A[6], _1_s_Comp[6]
  // _7486 7486_4: pin names not known; wires that end beside it: A[20], A[27], _1_s_Comp[20], A[21], A[27], _1_s_Comp[21], A[27], A[23], _1_s_Comp[23], A[27], A[22], _1_s_Comp[22]
  // _7486 7486_5: pin names not known; wires that end beside it: A[8], A[27], _1_s_Comp[8], A[9], A[27], _1_s_Comp[9], A[27], A[11], _1_s_Comp[11], A[27], A[10], _1_s_Comp[10]
  // _7486 7486_6: pin names not known; wires that end beside it: A[24], A[27], _1_s_Comp[24], A[25], A[27], _1_s_Comp[25], A[27], A[26], _1_s_Comp[26], A[27]
  Adder #(.width(27)) adder_1 (.a(_1_s_Comp), .b(bit_extender_1_out), .out(ABS), .cin(A[27]));  // open: cout
  assign bit_extender_1_out = {{26{1'b0}}, 1'b0};  // Bit_Extender bit_extender_1
  // _7486 7486_7: pin names not known; wires that end beside it: A[12], A[27], _1_s_Comp[12], A[13], A[27], _1_s_Comp[13], A[27], A[15], _1_s_Comp[15], A[27], A[14], _1_s_Comp[14]
  // Probe on ABS

  // Other names for the same wires on the sheet: Y0 = _1_s_Comp[0]; Y1 = _1_s_Comp[1]; Y2 = _1_s_Comp[2];
  //   Y3 = _1_s_Comp[3]; Y4 = _1_s_Comp[4]; Y5 = _1_s_Comp[5]; Y6 = _1_s_Comp[6]; Y7 = _1_s_Comp[7];
  //   Y8 = _1_s_Comp[8]; Y9 = _1_s_Comp[9]; Y10 = _1_s_Comp[10]; Y11 = _1_s_Comp[11]; Y12 = _1_s_Comp[12];
  //   Y13 = _1_s_Comp[13]; Y14 = _1_s_Comp[14]; Y15 = _1_s_Comp[15]; Y16 = _1_s_Comp[16]; Y17 = _1_s_Comp[17];
  //   Y18 = _1_s_Comp[18]; Y19 = _1_s_Comp[19]; Y20 = _1_s_Comp[20]; Y21 = _1_s_Comp[21]; Y22 = _1_s_Comp[22];
  //   Y23 = _1_s_Comp[23]; Y24 = _1_s_Comp[24]; Y25 = _1_s_Comp[25]; Y26 = _1_s_Comp[26]; Sign = A[27]
endmodule

module ExceptionThrower (
  input  [31:0] Input_32_bits,
  output out_2
);

  wire Not_One_out_2;

  OneChecker Not_One (.in_1(Input_32_bits[30:22]), .out_2(Not_One_out_2));
  not not_1 (out_2, Not_One_out_2);
endmodule

module OneChecker (
  input  [8:0] in_1,
  output out_2
);

  wire or_1_out;

  not not_1 (out_2, or_1_out);
  or or_1 (or_1_out, ~in_1[0], ~in_1[1], ~in_1[2], ~in_1[3], ~in_1[4], ~in_1[5], ~in_1[6], ~in_1[7], ~in_1[8]);  // OR_Gate

  // Other names for the same wires on the sheet: E0 = in_1[0]; E1 = in_1[1]; E2 = in_1[2]; E3 = in_1[3]; E4 = in_1[4];
  //   E5 = in_1[5]; E6 = in_1[6]; E7 = in_1[7]; E8 = in_1[8]
endmodule

// Zero
module ZeroCheckerExponent (
  input  [8:0] I,
  output out_2
);

  wire or_1_out;

  or or_1 (or_1_out, I[0], I[1], I[2], I[3], I[4], I[5], I[6], I[7], I[8]);
  not not_1 (out_2, or_1_out);

  // Other names for the same wires on the sheet: E0 = I[0]; E1 = I[1]; E2 = I[2]; E3 = I[3]; E4 = I[4]; E5 = I[5];
  //   E6 = I[6]; E7 = I[7]; E8 = I[8]
endmodule

module ZeroCheckerFraction (
  input  [21:0] I,
  output out_2
);

  wire n7432_1_p3, n7432_1_p6, n7432_1_p8, n7432_1_p9, n7432_2_p3, n7432_2_p6, n7432_2_p8, n7432_2_p9,
       n7432_3_p3, n7432_3_p6, n7432_3_p8, n7432_3_p9, n7432_4_p3, n7432_4_p6, n7432_4_p8, n7432_4_p9,
       n7432_5_p3, n7432_5_p6, n7432_5_p8, n7432_5_p9, or_1_out;

  // _7432 7432_1: pin names not known; wires that end beside it: I[0], I[1], n7432_1_p3, n7432_1_p3, I[2], n7432_1_p6, I[3], n7432_1_p8, n7432_1_p9, I[4], n7432_1_p6, n7432_1_p8
  // _7432 7432_2: pin names not known; wires that end beside it: n7432_1_p9, I[5], n7432_2_p3, n7432_2_p3, I[6], n7432_2_p6, I[7], n7432_2_p8, n7432_2_p9, I[8], n7432_2_p6, n7432_2_p8
  // _7432 7432_3: pin names not known; wires that end beside it: n7432_2_p9, I[9], n7432_3_p3, n7432_3_p3, I[10], n7432_3_p6, I[11], n7432_3_p8, n7432_3_p9, I[12], n7432_3_p6, n7432_3_p8
  // _7432 7432_4: pin names not known; wires that end beside it: n7432_3_p9, I[13], n7432_4_p3, n7432_4_p3, I[14], n7432_4_p6, I[15], n7432_4_p8, n7432_4_p9, I[16], n7432_4_p6, n7432_4_p8
  // _7432 7432_5: pin names not known; wires that end beside it: n7432_4_p9, I[17], n7432_5_p3, n7432_5_p3, I[18], n7432_5_p6, I[19], n7432_5_p8, n7432_5_p9, I[20], n7432_5_p6, n7432_5_p8
  or or_1 (or_1_out, I[21], n7432_5_p9);
  not not_1 (out_2, or_1_out);

  // Other names for the same wires on the sheet: F0 = I[0]; F1 = I[1]; F2 = I[2]; F3 = I[3]; F4 = I[4]; F5 = I[5];
  //   F6 = I[6]; F7 = I[7]; F8 = I[8]; F9 = I[9]; F10 = I[10]; F11 = I[11]; F12 = I[12]; F13 = I[13]; F14 = I[14];
  //   F15 = I[15]; F16 = I[16]; F17 = I[17]; F18 = I[18]; F19 = I[19]; F20 = I[20]; F21 = I[21]
endmodule
