// Logisim project MIPS.circ as structural Verilog: 16 circuits, main circuit main
module _8_bit_register (
  input  [3:0] readreg1,
  input  [3:0] readreg2,
  input  [3:0] writereg,
  input  [7:0] Write_Data,
  input  Clock,
  input  regWrite,
  input  Reset,
  output [7:0] Read_Data_1,
  output [7:0] zero,
  output [7:0] t0,
  output [7:0] t1,
  output [7:0] t2,
  output [7:0] t3,
  output [7:0] t4,
  output [7:0] sp,
  output [7:0] Read_Data_2
);

  wire and_1_out, and_2_out, and_3_out, and_4_out, and_5_out, and_6_out, and_7_out, decoder_1_out0,
       decoder_1_out1, decoder_1_out2, decoder_1_out3, decoder_1_out4, decoder_1_out5, decoder_1_out6;

  Decoder #(.select(3)) decoder_1 (
    .out0(decoder_1_out0), .out1(decoder_1_out1), .out2(decoder_1_out2), .out3(decoder_1_out3),
    .out4(decoder_1_out4), .out5(decoder_1_out5), .out6(decoder_1_out6), .sel(writereg[2:0]));  // open: out7, en
  and and_1 (and_1_out, decoder_1_out0, 1'b0);
  and and_2 (and_2_out, decoder_1_out1, regWrite);
  and and_3 (and_3_out, decoder_1_out2, regWrite);
  and and_4 (and_4_out, decoder_1_out3, regWrite);
  Register u_zero (.D(Write_Data), .en(and_1_out), .Q(zero), .clk(Clock), .clr(Reset));
  Register u_t0 (.D(Write_Data), .en(and_2_out), .Q(t0), .clk(Clock), .clr(Reset));
  Register u_t1 (.D(Write_Data), .en(and_3_out), .Q(t1), .clk(Clock), .clr(Reset));
  Register u_t2 (.D(Write_Data), .en(and_4_out), .Q(t2), .clk(Clock), .clr(Reset));
  and and_5 (and_5_out, decoder_1_out4, regWrite);
  and and_6 (and_6_out, decoder_1_out5, regWrite);
  and and_7 (and_7_out, decoder_1_out6, regWrite);
  Register u_t3 (.D(Write_Data), .en(and_5_out), .Q(t3), .clk(Clock), .clr(Reset));
  Register u_t4 (.D(Write_Data), .en(and_6_out), .Q(t4), .clk(Clock), .clr(Reset));
  Register u_sp (.D(Write_Data), .en(and_7_out), .Q(sp), .clk(Clock), .clr(Reset));
  Multiplexer #(.select(3), .width(8)) multiplexer_1 (
    .in0(zero), .in1(t0), .in2(t1), .in3(t2), .in4(t3), .in5(t4), .in6(sp), .out(Read_Data_1),
    .sel(readreg1[2:0]));  // open: in7, en
  Multiplexer #(.select(3), .width(8)) multiplexer_2 (
    .in0(zero), .in1(t0), .in2(t1), .in3(t2), .in4(t3), .in5(t4), .in6(sp), .out(Read_Data_2),
    .sel(readreg2[2:0]));  // open: in7, en
endmodule

module main (
  input  [12:0] in_1,
  input  in_2,
  input  [19:0] in_3,
  output [2:0] out_4,
  output [7:0] out_5,
  output [3:0] rs,
  output [3:0] rt,
  output [7:0] out_8,
  output [3:0] opcode,
  output [12:0] out_10,
  output [3:0] rd,
  output [1:0] out_12,
  output [7:0] out_13,
  output [12:0] out_14,
  output [7:0] out_15,
  output [7:0] out_16,
  output [1:0] out_17,
  output [12:0] out_18,
  output [12:0] out_19,
  output [7:0] out_20,
  output [7:0] out_21,
  output [12:0] out_22,
  output [12:0] out_23,
  output [7:0] sll_and_srl,
  output [7:0] out_25,
  output [7:0] out_26,
  output [7:0] out_27,
  output [7:0] out_28,
  output [7:0] out_29,
  output [7:0] out_30,
  output [19:0] out_31,
  output [19:0] out_32,
  output [7:0] out_33,
  output [7:0] out_34,
  output [7:0] out_35,
  output [7:0] out_36,
  output [7:0] out_37,
  output [7:0] out_38,
  output [3:0] out_39,
  output [7:0] out_40,
  output [7:0] out_41,
  output [3:0] out_42,
  output [3:0] out_43,
  output [3:0] out_44,
  output [7:0] out_45,
  output [2:0] out_46,
  output [3:0] out_47,
  output [3:0] out_48,
  output [7:0] out_49,
  output [3:0] out_50,
  output [15:0] out_51,
  output [7:0] out_52,
  output [7:0] out_53,
  output [7:0] t0,
  output [3:0] out_55,
  output [3:0] out_56,
  output [7:0] t1,
  output [1:0] out_58,
  output [3:0] out_59,
  output [7:0] t2,
  output [3:0] out_61,
  output [7:0] t3,
  output [3:0] out_63,
  output [7:0] t4,
  output [3:0] out_65,
  output [7:0] out_66,
  output [7:0] sp,
  output [3:0] out_68,
  output [15:0] out_69,
  output [15:0] out_70,
  output [15:0] out_71,
  output [15:0] out_72,
  output [3:0] out_73,
  output [15:0] out_74,
  output [3:0] out_75,
  output [3:0] out_76,
  output [3:0] out_77,
  output [3:0] out_78,
  output [3:0] out_79,
  output [3:0] out_80,
  output [7:0] out_81,
  output [7:0] out_82,
  output [7:0] out_83,
  output [7:0] out_84,
  output [7:0] out_85
);

  wire actual_branch_fwd, actual_jump, actual_stall, ALUSrc, and_4_out, and_5_out, and_8_out, and_9_out, beq,
       bne, brach_R_fwd_A, brach_R_fwd_B, Branch, BRANCH_FWD_L, BRANCH_FWD_R, branch_L_stall, branch_R_stall,
       branch_unit_1_branch, branch_unit_2_branch, CLK, comparator_1_eq, comparator_2_eq, fwd1, fwd2, Jump,
       JumpIF, LSForwarding, MemRead, MemRead_t, MemToReg, MemWrite, MemWrite_t, not_1_out, not_2_out,
       not_3_out, not_4_out, not_5_out, not_6_out, not_7_out, not_8_out, not_9_out, RegDst, RegWrite,
       Shifter, Stall, zero;
  wire [3:0] multiplexer_7_out, WriteRegEX;
  wire [7:0] adder_2_out, AForwarded, AForwardedFor_sll, B, jump_t, MEM_Result, multiplexer_1_out,
       multiplexer_3_out, multiplexer_4_out, multiplexer_21_out, Next_PC, PC, PC_4;
  wire [12:0] multiplexer_13_out;
  wire [19:0] Instruction_check, multiplexer_5_out;

  Register u_PC (.D(Next_PC), .Q(PC), .clk(CLK), .clr(in_2));  // open: en
  Clock clock_1 (.out(CLK));
  Multiplexer #(.width(8), .enable("false")) multiplexer_1 (
    .in0(8'h1), .in1({8{1'b0}}), .out(multiplexer_1_out), .sel(actual_stall));
  Adder adder_1 (.a(multiplexer_1_out), .b(PC), .out(PC_4));  // open: cin, cout
  not not_1 (not_1_out, actual_branch_fwd);
  RAM #(.dataWidth(20), .bus("asynch")) ram_1 (
    .addr(PC), .data({out_32[19:16], out_5, out_32[7:0]}), .sel(1'b1), .ld(1'b1));  // open: clr
  or or_1 (actual_branch_fwd, BRANCH_FWD_R, BRANCH_FWD_L);
  Adder adder_2 (.a(PC_4), .b(out_31[7:0]), .out(adder_2_out));  // open: cin, cout
  not not_2 (not_2_out, branch_L_stall);
  not not_3 (not_3_out, branch_R_stall);
  or or_2 (actual_stall, Stall, branch_R_stall, actual_branch_fwd, branch_L_stall);
  and and_1 (actual_jump, not_1_out, JumpIF, not_2_out, not_3_out);
  Multiplexer #(.width(20), .enable("false")) multiplexer_2 (
    .in0({opcode, out_31[15:0]}), .in1(in_3), .out(Instruction_check), .sel(actual_branch_fwd));
  Multiplexer #(.width(8), .enable("false")) multiplexer_3 (
    .in0(PC_4), .in1(adder_2_out), .out(multiplexer_3_out), .sel(actual_branch_fwd));
  Multiplexer #(.width(8), .enable("false")) multiplexer_4 (
    .in0(PC_4), .in1(out_16), .out(multiplexer_4_out), .sel(actual_stall));
  Multiplexer #(.width(20), .enable("false")) multiplexer_5 (
    .in0({out_32[19:16], out_5, out_32[7:0]}), .in1(Instruction_check), .out(multiplexer_5_out),
    .sel(actual_stall));
  Branch_L_Detect_Unit branch_l_detect_unit_1 (
    .IF_ID_RS(out_31[15:12]), .IF_ID_RT(out_31[11:8]), .ID_EX_MEMREAD(out_14[9]), .EX_MEM_MEMREAD(out_19[9]),
    .ID_EX_RD(WriteRegEX), .EX_MEM_RD(out_43), .IF_ID_BEQ(beq), .IF_ID_BNEQ(bne),
    .banch_stall_L(branch_L_stall));
  control_unit control_unit_1 (
    .OpCode(out_32[19:16]), .jump(JumpIF));  // open: ALUOP, bne, beq, MemWrite, MemToReg, RegWrite, MemRead, ALUSrc, RegDst, shifter, out_13
  IF_ID if_id_1 (
    .in_1(multiplexer_4_out), .in_2(multiplexer_5_out), .out_5(out_16), .out_6({opcode, out_31[15:0]}),
    .in_3(CLK), .reset(in_2));
  Multiplexer #(.width(8), .enable("false")) multiplexer_6 (
    .in0(multiplexer_3_out), .in1(out_5), .out(Next_PC), .sel(actual_jump));
  Multiplexer #(.width(4), .enable("false")) multiplexer_7 (
    .in0(out_39), .in1(out_42), .out(multiplexer_7_out), .sel(out_23[11]));
  Hazard_Detection_Unit hazard_detection_unit_1 (
    .IF_ID_RS(out_31[15:12]), .IF_ID_RT(out_31[11:8]), .ID_EX_MEMREAD(out_14[9]), .ID_EX_RT(out_61),
    .out_7(Stall), .ALUsrc(ALUSrc), .MemWrite(MemWrite));
  Branch_R_Forward branch_r_forward_1 (
    .IF_ID_RS(out_31[15:12]), .IF_ID_RT(out_31[11:8]), .EX_MEM_REGWRITE(out_19[8]), .EX_MEM_RD(out_43),
    .IF_ID_BEQ(beq), .IF_ID_BNEQ(bne), .forwardA(brach_R_fwd_A), .forwardB(brach_R_fwd_B));
  _8_bit_register u_8_bit_register_1 (
    .readreg2(out_31[11:8]), .writereg(multiplexer_7_out), .Write_Data(out_8), .Read_Data_1(out_27),
    .Read_Data_2(out_36), .regWrite(out_23[8]), .Clock(CLK), .Reset(in_2), .t0(t0), .t1(t1), .t2(t2),
    .t3(t3), .t4(t4), .sp(sp), .readreg1(out_31[15:12]));  // open: zero
  Multiplexer #(.width(4), .enable("false")) multiplexer_8 (
    .in0(out_31[11:8]), .in1(out_31[7:4]), .out(out_63), .sel(RegDst));
  Multiplexer #(.width(8), .enable("false")) multiplexer_9 (
    .in0(out_85), .in1(out_15), .out(out_82), .sel(brach_R_fwd_B));
  Multiplexer #(.width(8), .enable("false")) multiplexer_10 (.in0(out_36), .in1(out_8), .out(out_85), .sel(fwd2));
  Multiplexer #(.width(8), .enable("false")) multiplexer_11 (.in0(out_27), .in1(out_8), .out(out_84), .sel(fwd1));
  control_unit control_unit_2 (
    .OpCode(opcode), .jump(Jump), .ALUOP(out_4), .bne(bne), .beq(beq), .MemWrite(MemWrite),
    .MemToReg(MemToReg), .RegWrite(RegWrite), .MemRead(MemRead), .ALUSrc(ALUSrc), .RegDst(RegDst),
    .shifter(Shifter), .out_13(out_10));
  Multiplexer #(.width(8), .enable("false")) multiplexer_12 (
    .in0(out_84), .in1(out_15), .out(out_81), .sel(brach_R_fwd_A));
  RAAAW_Unit raaaw_unit_1 (
    .MEM_WB_RD(out_76), .MEM_WB_REGWRITE(out_23[8]), .IF_ID_RT(out_31[11:8]), .IF_ID_RS(out_31[15:12]),
    .ALU_src(ALUSrc), .MemWrite(MemWrite), .forwardA(fwd1), .forwardB(fwd2));
  Branch_R_Detect_Unit branch_r_detect_unit_1 (
    .IF_ID_RS(out_31[15:12]), .IF_ID_RT(out_31[11:8]), .ID_EX_REGWRITE(out_14[8]), .ID_EX_RD(WriteRegEX),
    .IF_ID_BEQ(beq), .IF_ID_BNEQ(bne), .branch_stall_R(branch_R_stall), .ALUsrc(ALUSrc));
  Comparator comparator_1 (.a(out_81), .b(out_82), .eq(comparator_1_eq));  // open: gt, lt
  Comparator comparator_2 (.a(out_84), .b(out_85), .eq(comparator_2_eq));  // open: gt, lt
  branch_unit branch_unit_1 (.zero(comparator_2_eq), .beq(beq), .bne(bne), .branch(branch_unit_1_branch));
  branch_unit branch_unit_2 (.zero(comparator_1_eq), .beq(beq), .bne(bne), .branch(branch_unit_2_branch));
  Multiplexer #(.width(13), .enable("false")) multiplexer_13 (
    .in0(out_10), .in1(in_1), .out(multiplexer_13_out), .sel(Stall));
  not not_4 (not_4_out, branch_R_stall);
  not not_5 (not_5_out, branch_L_stall);
  not not_6 (not_6_out, branch_R_stall);
  not not_7 (not_7_out, branch_L_stall);
  // ID_EX id_ex_1: pin names not known; wires that end beside it: multiplexer_13_out, out_16, out_84, out_85, out_31[7:0], out_63, out_31[15:8], out_31[15:0], CLK, in_2, out_14, out_25, out_34, out_40, out_66, WriteRegEX, jump_t, {out_65, out_61, out_50, out_66[3:0]}
  and and_2 (BRANCH_FWD_R, branch_unit_2_branch, not_4_out, not_5_out);
  and and_3 (BRANCH_FWD_L, branch_unit_1_branch, not_6_out, not_7_out, out_23[9]);
  branch_unit branch_unit_3 (.zero(zero), .beq(beq), .bne(bne), .branch(Branch));
  Forwarding_Unit forwarding_unit_1 (
    .forwardA(out_12), .MEM_WB_RD(out_76), .EX_MEM_RD(out_43), .ALU_src(out_14[10]), .forwardB(out_58),
    .MEM_WB_REGWRITE(out_23[8]), .ID_EX_RS(out_65), .ID_EX_RT(out_61), .EX_MEM_REGWRITE(out_19[8]),
    .MemWrite(out_14[6]));
  assign sll_and_srl = {{4{1'b0}}, out_66[3:0]};  // Bit_Extender bit_extender_1
  Multiplexer #(.width(8), .enable("false")) multiplexer_14 (.in0(B), .in1(out_66), .out(out_53), .sel(out_14[10]));
  Multiplexer #(.width(8), .enable("false")) multiplexer_15 (
    .in0(out_34), .in1(sll_and_srl), .out(out_29), .sel(out_14[12]));
  Multiplexer #(.width(8), .enable("false")) multiplexer_16 (
    .in0(AForwarded), .in1(out_29), .out(out_35), .sel(out_14[12]));
  Multiplexer #(.width(8), .enable("false")) multiplexer_17 (
    .in0(out_53), .in1(AForwardedFor_sll), .out(out_45), .sel(out_14[12]));
  Multiplexer #(.select(2), .width(8), .enable("false")) multiplexer_18 (
    .in0(out_34), .in1(out_8), .in2(out_15), .out(AForwardedFor_sll), .sel(out_12));  // open: in3
  Multiplexer #(.select(2), .width(8), .enable("false")) multiplexer_19 (
    .in0(out_40), .in1(out_8), .in2(out_15), .out(B), .sel(out_58));  // open: in3
  // ALU_8_by_ART alu_8_by_art_1: pin names not known; wires that end beside it: out_35, out_45, out_14[3:1], zero, out_30
  Multiplexer #(.select(2), .width(8), .enable("false")) multiplexer_20 (
    .in0(out_29), .in1(out_8), .in2(out_15), .out(AForwarded), .sel(out_12));  // open: in3
  EX_MEM ex_mem_1 (
    .in_1(out_14), .in_2(out_25), .in_3(zero), .in_4(out_30), .in_6(B), .out_11(out_19), .out_12(out_26),
    .out_14(out_15), .out_16(out_20), .in_9(CLK), .in_8({out_65, out_61, out_50, out_66[3:0]}),
    .out_18({out_51[15:8], out_47, out_51[3:0]}), .out_17(out_43), .in_7(WriteRegEX), .reset(in_2));  // open: in_5, out_13, out_15
  and and_4 (and_4_out, out_51[13], out_51[14]);
  and and_5 (and_5_out, out_51[13], out_51[14]);
  Multiplexer #(.width(8), .enable("false")) multiplexer_21 (
    .in0(out_20), .in1(out_13), .out(multiplexer_21_out), .sel(LSForwarding));
  and and_6 (MemWrite_t, out_19[6], and_4_out);
  and and_7 (MemRead_t, out_19[9], and_5_out);
  Multiplexer #(.width(8), .enable("false")) multiplexer_22 (
    .in0(out_20), .in1(out_13), .out(out_21), .sel(LSForwarding));
  not not_8 (not_8_out, MemWrite_t);
  and and_8 (and_8_out, out_19[6], not_8_out);
  Load_Store_Forwarding load_store_forwarding_1 (
    .rtWB(out_39), .rtMEM(out_51[11:8]), .MemWriteMEM(out_19[6]), .MemReadWB(out_19[9]),
    .forward(LSForwarding));
  RAM #(.bus("separate")) ram_2 (
    .addr(out_15), .din(out_21), .data(MEM_Result), .str(and_8_out), .sel(1'b1), .clk(CLK), .ld(and_9_out),
    .clr(in_2));
  RAM #(.bus("separate")) ram_3 (
    .addr(out_15), .din(multiplexer_21_out), .data(MEM_Result), .str(MemWrite_t), .sel(1'b1), .clk(CLK),
    .ld(MemRead_t), .clr(in_2));
  and and_9 (and_9_out, not_9_out, out_19[9]);
  not not_9 (not_9_out, MemRead_t);
  MEM_WB mem_wb_1 (
    .in_1(out_19), .in_4(out_15), .in_5(MEM_Result), .out_11(out_23), .out_14(out_41), .out_15(out_13),
    .in_9(CLK), .in_8({out_51[15:8], out_47, out_51[3:0]}),
    .out_18({out_72[15:12], out_39, out_42, out_72[3:0]}), .in_7(out_43), .out_17(out_76), .reset(in_2));  // open: in_2, in_3, in_6, out_12, out_13, out_16
  Multiplexer #(.width(8), .enable("false")) multiplexer_23 (.in0(out_41), .in1(out_13), .out(out_8), .sel(out_23[7]));

  assign out_17 = out_12;
  assign out_18 = out_14;
  assign out_22 = out_19;
  assign out_28 = out_25;
  assign out_31[19:16] = opcode;
  assign out_32[15:8] = out_5;
  assign out_33 = out_16;
  assign out_37 = out_15;
  assign out_38 = out_8;
  assign out_44 = out_31[15:12];
  assign out_46 = out_14[3:1];
  assign out_48 = out_31[11:8];
  assign out_49 = out_15;
  assign out_51[7:4] = out_47;
  assign out_52 = out_8;
  assign out_55 = out_51[11:8];
  assign out_56 = out_31[7:4];
  assign out_59 = out_31[11:8];
  assign out_68 = out_51[11:8];
  assign out_69 = {out_65, out_61, out_50, out_66[3:0]};
  assign out_70 = {out_51[15:8], out_47, out_51[3:0]};
  assign out_71 = {out_65, out_61, out_50, out_66[3:0]};
  assign out_72[11:4] = {out_39, out_42};
  assign out_73 = out_43;
  assign out_74 = out_31[15:0];
  assign out_75 = out_31[7:4];
  assign out_77 = out_76;
  assign out_78 = out_51[15:12];
  assign out_79 = out_43;
  assign out_80 = out_61;
  assign out_83 = out_15;
  assign rd = out_31[7:4];
  assign rs = out_31[15:12];
  assign rt = out_31[11:8];

  // Other names for the same wires on the sheet: Instruction_ID[19:0] = {opcode, out_31[15:0]};
  //   Shamt[3:0] = out_31[3:0]; A[7:0] = out_29; addi_imme[7:0] = out_66; Address[7:0] = out_30;
  //   AddressMEM[7:0] = out_15; AddressWB[7:0] = out_41; ALUOp[2:0] = out_4; BForwarded[7:0] = out_53;
  //   controls[12:0] = out_10; ControlsEx[12:0] = out_14; JumpEX = out_14[0]; ALUOpEX[2:0] = out_14[3:1];
  //   bneEX = out_14[4]; beqEX = out_14[5]; MemWriteEX = out_14[6]; MemToRegEX = out_14[7]; RegWriteEX = out_14[8];
  //   MemReadEX = out_14[9]; ALUSrcEX = out_14[10]; RegDstEX = out_14[11]; ShifterEX = out_14[12];
  //   ControlsMEM[12:0] = out_19; JumpMEM = out_19[0]; ALUOpMEM[2:0] = out_19[3:1]; bneMEM = out_19[4];
  //   beqMEM = out_19[5]; MemWriteMEM = out_19[6]; MemToRegMEM = out_19[7]; RegWriteMEM = out_19[8];
  //   MemReadMEM = out_19[9]; ALUSrcMEM = out_19[10]; RegDstMEM = out_19[11]; ShifterMEM = out_19[12];
  //   ControlsWB[12:0] = out_23; JumpWB = out_23[0]; ALUOpWB[2:0] = out_23[3:1]; bneWB = out_23[4]; beqWB = out_23[5];
  //   MemWriteWB = out_23[6]; MemToRegWB = out_23[7]; RegWriteWB = out_23[8]; MemReadWB = out_23[9];
  //   ALUSrcWB = out_23[10]; RegDstWB = out_23[11]; ShifterWB = out_23[12]; ForwordA[1:0] = out_12;
  //   ForwordB[1:0] = out_58; Instruction[19:0] = {out_32[19:16], out_5, out_32[7:0]}; OpCode_IF[3:0] = out_32[19:16];
  //   Jump_IF[7:0] = out_5; MEM_ResultWB[7:0] = out_13; ShamtMEM[3:0] = out_51[3:0]; rdMEM[3:0] = out_47;
  //   rtMEM[3:0] = out_51[11:8]; rsMEM[3:0] = out_51[15:12]; ShamtEX[3:0] = out_66[3:0]; rdEX[3:0] = out_50;
  //   rtEX[3:0] = out_61; rsEX[3:0] = out_65; ShamtWB[3:0] = out_72[3:0]; rdWB[3:0] = out_42; rtWB[3:0] = out_39;
  //   rsWB[3:0] = out_72[15:12]; PC_4_EX[7:0] = out_25; PC_4_ID[7:0] = out_16; PC_4_MEM[7:0] = out_26;
  //   RAAAW_read_data_1[7:0] = out_84; RAAAW_read_data_2[7:0] = out_85; Read_Data_1[7:0] = out_27;
  //   Read_Data_1_EX[7:0] = out_34; Read_Data_2[7:0] = out_36; Read_Data_2_EX[7:0] = out_40;
  //   Read_Data_2_MEM[7:0] = out_20; Reset = in_2; Write_Data[7:0] = out_8; WriteReg[3:0] = out_63;
  //   WriteRegMEM[3:0] = out_43; WriteRegWB[3:0] = out_76

  // Notes on the sheet:
  //   Instruction Fetch
  //   Instruction Memory 
  //   pc+4
  //   branch check
  //   Controller
  //   jump check
  //   Reg
  //   branch logic
  //   Data Memory
  //   SP memory
endmodule

module control_unit (
  input  [3:0] OpCode,
  output jump,
  output [2:0] ALUOP,
  output bne,
  output beq,
  output MemWrite,
  output MemToReg,
  output RegWrite,
  output MemRead,
  output ALUSrc,
  output RegDst,
  output shifter,
  output [12:0] out_13
);

  wire or_1_out;

  ROM #(.addrWidth(4), .dataWidth(12)) rom_1 (
    .addr(OpCode), .data({out_13[11], ALUSrc, MemRead, out_13[8], MemToReg, MemWrite, beq, bne, ALUOP, jump}));  // open: sel
  or or_1 (or_1_out, ALUOP[0], ALUOP[1]);
  and and_1 (out_13[12], or_1_out, ALUOP[2]);

  assign {out_13[10:9], out_13[7:0]} = {ALUSrc, MemRead, MemToReg, MemWrite, beq, bne, ALUOP, jump};
  assign RegDst = out_13[11];
  assign RegWrite = out_13[8];
  assign shifter = out_13[12];

  // Notes on the sheet:
  //   contents of rom_1 (hex, n*v repeats v):
  //   506 500 904 90a 502 908 780 900 12 440 902 504 1 906 22 90c
endmodule

module branch_unit (
  input  zero,
  input  beq,
  input  bne,
  output branch
);

  wire and_1_out, and_2_out, not_1_out;

  and and_1 (and_1_out, zero, beq);
  not not_1 (not_1_out, zero);
  and and_2 (and_2_out, not_1_out, bne);
  or or_1 (branch, and_1_out, and_2_out);
endmodule

module IF_ID (
  input  [7:0] in_1,
  input  [19:0] in_2,
  input  in_3,
  input  reset,
  output [7:0] out_5,
  output [19:0] out_6
);

  Register PC_4 (.D(in_1), .Q(out_5), .clk(in_3), .clr(reset));  // open: en
  Register #(.width(20)) instructions (.D(in_2), .Q(out_6), .clk(in_3), .clr(reset));  // open: en
endmodule

module ID_EX (
  input  [12:0] in_1,
  input  [7:0] in_2,
  input  [7:0] in_3,
  input  [7:0] in_4,
  input  [7:0] in_5,
  input  [7:0] in_6,
  input  [3:0] in_7,
  input  [15:0] in_8,
  input  in_9,
  input  reset,
  output [12:0] out_11,
  output [7:0] out_12,
  output [7:0] out_13,
  output [7:0] out_14,
  output [7:0] out_15,
  output [7:0] out_16,
  output [3:0] out_17,
  output [15:0] out_18
);

  Register #(.width(13)) ControlBits (.D(in_1), .Q(out_11), .clk(in_9), .clr(reset));  // open: en
  Register PC_4 (.D(in_2), .Q(out_12), .clk(in_9), .clr(reset));  // open: en
  Register Reg1_Data (.D(in_3), .Q(out_13), .clk(in_9), .clr(reset));  // open: en
  Register Reg2_Data (.D(in_4), .Q(out_14), .clk(in_9));  // open: en, clr
  Register addr_imme (.D(in_5), .Q(out_15), .clk(in_9), .clr(reset));  // open: en
  Register Jump (.D(in_6), .Q(out_16), .clk(in_9), .clr(reset));  // open: en
  Register #(.width(4)) WriteReg (.D(in_7), .Q(out_17), .clk(in_9), .clr(reset));  // open: en
  Register #(.width(16)) Intstructions (.D(in_8), .Q(out_18), .clk(in_9), .clr(reset));  // open: en
endmodule

module EX_MEM (
  input  [12:0] in_1,
  input  [7:0] in_2,
  input  in_3,
  input  [7:0] in_4,
  input  [7:0] in_5,
  input  [7:0] in_6,
  input  [3:0] in_7,
  input  [15:0] in_8,
  input  in_9,
  input  reset,
  output [12:0] out_11,
  output [7:0] out_12,
  output out_13,
  output [7:0] out_14,
  output [7:0] out_15,
  output [7:0] out_16,
  output [3:0] out_17,
  output [15:0] out_18
);

  Register #(.width(13)) ControlBits (.D(in_1), .Q(out_11), .clk(in_9), .clr(reset));  // open: en
  Register PC_4 (.D(in_2), .Q(out_12), .clk(in_9), .clr(reset));  // open: en
  Register #(.width(1)) ZERO (.D(in_3), .Q(out_13), .clk(in_9), .clr(reset));  // open: en
  Register ALU_Result (.D(in_4), .Q(out_14), .clk(in_9), .clr(reset));  // open: en
  Register addr_imme (.D(in_5), .Q(out_15), .clk(in_9), .clr(reset));  // open: en
  Register Read_Data_2 (.D(in_6), .Q(out_16), .clk(in_9), .clr(reset));  // open: en
  Register #(.width(4)) WriteReg (.D(in_7), .Q(out_17), .clk(in_9), .clr(reset));  // open: en
  Register #(.width(16)) Intstructions (.D(in_8), .Q(out_18), .clk(in_9), .clr(reset));  // open: en
endmodule

module MEM_WB (
  input  [12:0] in_1,
  input  [7:0] in_2,
  input  in_3,
  input  [7:0] in_4,
  input  [7:0] in_5,
  input  [7:0] in_6,
  input  [3:0] in_7,
  input  [15:0] in_8,
  input  in_9,
  input  reset,
  output [12:0] out_11,
  output [7:0] out_12,
  output out_13,
  output [7:0] out_14,
  output [7:0] out_15,
  output [7:0] out_16,
  output [3:0] out_17,
  output [15:0] out_18
);

  Register #(.width(13)) ControlBits (.D(in_1), .Q(out_11), .clk(in_9), .clr(reset));  // open: en
  Register PC_4 (.D(in_2), .Q(out_12), .clk(in_9), .clr(reset));  // open: en
  Register #(.width(1)) ZERO (.D(in_3), .Q(out_13), .clk(in_9), .clr(reset));  // open: en
  Register ALU_Result (.D(in_4), .Q(out_14), .clk(in_9), .clr(reset));  // open: en
  Register memResult (.D(in_5), .Q(out_15), .clk(in_9), .clr(reset));  // open: en
  Register Jump (.D(in_6), .Q(out_16), .clk(in_9), .clr(reset));  // open: en
  Register #(.width(4)) WriteReg (.D(in_7), .Q(out_17), .clk(in_9), .clr(reset));  // open: en
  Register #(.width(16)) Intstructions (.D(in_8), .Q(out_18), .clk(in_9), .clr(reset));  // open: en
endmodule

module Forwarding_Unit (
  input  [3:0] MEM_WB_RD,
  input  MEM_WB_REGWRITE,
  input  [3:0] ID_EX_RT,
  input  EX_MEM_REGWRITE,
  input  [3:0] EX_MEM_RD,
  input  [3:0] ID_EX_RS,
  input  ALU_src,
  input  MemWrite,
  output [1:0] forwardA,
  output [1:0] forwardB
);

  wire and_1_out, and_2_out, and_3_out, and_4_out, and_5_out, and_6_out, comparator_1_eq, comparator_2_eq,
       comparator_3_eq, comparator_4_eq, comparator_5_eq, comparator_6_eq, comparator_7_eq, comparator_8_eq,
       EX_MEM_forwarding_A, EX_MEM_forwarding_B, MEM_WB_forwarding_A, MEM_WB_forwarding_B, not_1_out,
       not_2_out, not_3_out, not_4_out, not_5_out, not_6_out, or_1_out, or_2_out;

  not not_1 (not_1_out, ALU_src);
  Comparator #(.width(4)) comparator_1 (.a(EX_MEM_RD), .b(ID_EX_RT), .eq(comparator_1_eq));  // open: gt, lt
  Comparator #(.width(4)) comparator_2 (.a(MEM_WB_RD), .b(ID_EX_RS), .eq(comparator_2_eq));  // open: gt, lt
  Comparator #(.width(4)) comparator_3 (.a(EX_MEM_RD), .b(4'b0000), .eq(comparator_3_eq));  // open: gt, lt
  Comparator #(.width(4)) comparator_4 (.a(EX_MEM_RD), .b(ID_EX_RS), .eq(comparator_4_eq));  // open: gt, lt
  Comparator #(.width(4)) comparator_5 (.a(MEM_WB_RD), .b(4'b0000), .eq(comparator_5_eq));  // open: gt, lt
  not not_2 (not_2_out, ALU_src);
  or or_1 (or_1_out, not_2_out, MemWrite);
  Comparator #(.width(4)) comparator_6 (.a(MEM_WB_RD), .b(ID_EX_RT), .eq(comparator_6_eq));  // open: gt, lt
  not not_3 (not_3_out, comparator_7_eq);
  Comparator #(.width(4)) comparator_7 (.a(EX_MEM_RD), .b(4'b0000), .eq(comparator_7_eq));  // open: gt, lt
  or or_2 (or_2_out, not_1_out, MemWrite);
  Comparator #(.width(4)) comparator_8 (.a(MEM_WB_RD), .b(4'b0000), .eq(comparator_8_eq));  // open: gt, lt
  not not_4 (not_4_out, comparator_8_eq);
  not not_5 (not_5_out, comparator_3_eq);
  not not_6 (not_6_out, comparator_5_eq);
  and and_1 (and_1_out, or_1_out, comparator_6_eq);
  and and_2 (and_2_out, or_2_out, comparator_1_eq);
  and and_3 (and_3_out, EX_MEM_REGWRITE, and_2_out);
  and and_4 (and_4_out, MEM_WB_REGWRITE, comparator_2_eq);
  and and_5 (and_5_out, EX_MEM_REGWRITE, comparator_4_eq);
  and and_6 (and_6_out, MEM_WB_REGWRITE, and_1_out);
  and and_7 (EX_MEM_forwarding_A, not_5_out, and_5_out);
  and and_8 (MEM_WB_forwarding_B, not_6_out, and_6_out);
  and and_9 (EX_MEM_forwarding_B, not_3_out, and_3_out);
  and and_10 (MEM_WB_forwarding_A, not_4_out, and_4_out);
  Priority_Encoder #(.select(2)) priority_encoder_1 (
    .in0(1'b1), .in1(MEM_WB_forwarding_A), .in2(EX_MEM_forwarding_A), .out(forwardA));  // open: in3, gs, en_out, en_in
  Priority_Encoder #(.select(2)) priority_encoder_2 (
    .in0(1'b1), .in1(MEM_WB_forwarding_B), .in2(EX_MEM_forwarding_B), .out(forwardB));  // open: in3, gs, en_out, en_in

  // Other names for the same wires on the sheet: ALUsrc = ALU_src
endmodule

module Hazard_Detection_Unit (
  input  [3:0] IF_ID_RS,
  input  [3:0] IF_ID_RT,
  input  ID_EX_MEMREAD,
  input  [3:0] ID_EX_RT,
  input  ALUsrc,
  input  MemWrite,
  output out_7
);

  wire and_1_out, comparator_1_eq, comparator_2_eq, not_1_out, or_1_out, or_2_out;

  not not_1 (not_1_out, ALUsrc);
  or or_1 (or_1_out, not_1_out, MemWrite);
  Comparator #(.width(4)) comparator_1 (.a(IF_ID_RT), .b(ID_EX_RT), .eq(comparator_1_eq));  // open: gt, lt
  Comparator #(.width(4)) comparator_2 (.a(IF_ID_RS), .b(ID_EX_RT), .eq(comparator_2_eq));  // open: gt, lt
  and and_1 (and_1_out, or_1_out, comparator_1_eq);
  or or_2 (or_2_out, comparator_2_eq, and_1_out);
  and and_2 (out_7, ID_EX_MEMREAD, or_2_out);
endmodule

module Load_Store_Forwarding (
  input  [3:0] rtWB,
  input  [3:0] rtMEM,
  input  MemWriteMEM,
  input  MemReadWB,
  output forward
);

  wire comparator_1_eq;

  Comparator #(.width(4)) comparator_1 (.a(rtWB), .b(rtMEM), .eq(comparator_1_eq));  // open: gt, lt
  and and_1 (forward, comparator_1_eq, MemWriteMEM, MemReadWB);
endmodule

module RAAAW_Unit (
  input  [3:0] MEM_WB_RD,
  input  MEM_WB_REGWRITE,
  input  [3:0] IF_ID_RT,
  input  [3:0] IF_ID_RS,
  input  ALU_src,
  input  MemWrite,
  output forwardA,
  output forwardB
);

  wire and_1_out, and_2_out, and_3_out, comparator_1_eq, comparator_2_eq, comparator_3_eq, comparator_4_eq,
       not_1_out, not_2_out, not_3_out, or_1_out, RAAAW_A, RAAAW_B;

  not not_1 (not_1_out, ALU_src);
  Comparator #(.width(4)) comparator_1 (.a(MEM_WB_RD), .b(IF_ID_RT), .eq(comparator_1_eq));  // open: gt, lt
  Comparator #(.width(4)) comparator_2 (.a(MEM_WB_RD), .b(IF_ID_RS), .eq(comparator_2_eq));  // open: gt, lt
  not not_2 (not_2_out, comparator_3_eq);
  Comparator #(.width(4)) comparator_3 (.a(MEM_WB_RD), .b(4'b0000), .eq(comparator_3_eq));  // open: gt, lt
  or or_1 (or_1_out, not_1_out, MemWrite);
  Comparator #(.width(4)) comparator_4 (.a(MEM_WB_RD), .b(4'b0000), .eq(comparator_4_eq));  // open: gt, lt
  not not_3 (not_3_out, comparator_4_eq);
  and and_1 (and_1_out, or_1_out, comparator_1_eq);
  and and_2 (and_2_out, MEM_WB_REGWRITE, and_1_out);
  and and_3 (and_3_out, MEM_WB_REGWRITE, comparator_2_eq);
  and and_4 (RAAAW_B, not_2_out, and_2_out);
  and and_5 (RAAAW_A, not_3_out, and_3_out);
  Priority_Encoder #(.select(1)) priority_encoder_1 (
    .in0(1'b1), .in1(RAAAW_A), .out(forwardA));  // open: gs, en_out, en_in
  Priority_Encoder #(.select(1)) priority_encoder_2 (
    .in0(1'b1), .in1(RAAAW_B), .out(forwardB));  // open: gs, en_out, en_in

  // Other names for the same wires on the sheet: ALUsrc = ALU_src
endmodule

module Branch_R_Detect_Unit (
  input  [3:0] IF_ID_RS,
  input  [3:0] IF_ID_RT,
  input  ID_EX_REGWRITE,
  input  [3:0] ID_EX_RD,
  input  IF_ID_BEQ,
  input  IF_ID_BNEQ,
  input  ALUsrc,
  output branch_stall_R
);

  wire comparator_1_eq, comparator_2_eq, comparator_3_eq, not_1_out, not_2_out, or_1_out, or_2_out;

  Comparator #(.width(4)) comparator_1 (.a(ID_EX_RD), .b(4'b0000), .eq(comparator_1_eq));  // open: gt, lt
  Comparator #(.width(4)) comparator_2 (.a(IF_ID_RS), .b(ID_EX_RD), .eq(comparator_2_eq));  // open: gt, lt
  Comparator #(.width(4)) comparator_3 (.a(IF_ID_RT), .b(ID_EX_RD), .eq(comparator_3_eq));  // open: gt, lt
  or or_1 (or_1_out, IF_ID_BEQ, IF_ID_BNEQ);
  not not_1 (not_1_out, comparator_1_eq);
  not not_2 (not_2_out, ALUsrc);
  or or_2 (or_2_out, comparator_2_eq, comparator_3_eq);
  and and_1 (branch_stall_R, or_2_out, or_1_out, not_1_out, ID_EX_REGWRITE, not_2_out);
endmodule

module Branch_L_Detect_Unit (
  input  [3:0] IF_ID_RS,
  input  [3:0] IF_ID_RT,
  input  ID_EX_MEMREAD,
  input  EX_MEM_MEMREAD,
  input  [3:0] ID_EX_RD,
  input  [3:0] EX_MEM_RD,
  input  IF_ID_BEQ,
  input  IF_ID_BNEQ,
  output banch_stall_L
);

  wire and_1_out, and_2_out, comparator_1_eq, comparator_2_eq, comparator_3_eq, comparator_4_eq,
       comparator_5_eq, comparator_6_eq, not_1_out, not_2_out, or_1_out, or_2_out, or_3_out, or_4_out;

  Comparator #(.width(4)) comparator_1 (.a(ID_EX_RD), .b(4'b0000), .eq(comparator_1_eq));  // open: gt, lt
  Comparator #(.width(4)) comparator_2 (.a(EX_MEM_RD), .b(4'b0000), .eq(comparator_2_eq));  // open: gt, lt
  Comparator #(.width(4)) comparator_3 (.a(IF_ID_RS), .b(ID_EX_RD), .eq(comparator_3_eq));  // open: gt, lt
  Comparator #(.width(4)) comparator_4 (.a(IF_ID_RT), .b(ID_EX_RD), .eq(comparator_4_eq));  // open: gt, lt
  or or_1 (or_1_out, IF_ID_BEQ, IF_ID_BNEQ);
  not not_1 (not_1_out, comparator_1_eq);
  Comparator #(.width(4)) comparator_5 (.a(IF_ID_RS), .b(EX_MEM_RD), .eq(comparator_5_eq));  // open: gt, lt
  Comparator #(.width(4)) comparator_6 (.a(IF_ID_RT), .b(EX_MEM_RD), .eq(comparator_6_eq));  // open: gt, lt
  or or_2 (or_2_out, IF_ID_BEQ, IF_ID_BNEQ);
  not not_2 (not_2_out, comparator_2_eq);
  or or_3 (or_3_out, comparator_3_eq, comparator_4_eq);
  or or_4 (or_4_out, comparator_5_eq, comparator_6_eq);
  and and_1 (and_1_out, or_3_out, or_1_out, not_1_out, ID_EX_MEMREAD);
  and and_2 (and_2_out, or_4_out, or_2_out, not_2_out, EX_MEM_MEMREAD);
  or or_5 (banch_stall_L, and_1_out, and_2_out);
endmodule

module Branch_R_Forward (
  input  [3:0] IF_ID_RS,
  input  [3:0] IF_ID_RT,
  input  EX_MEM_REGWRITE,
  input  [3:0] EX_MEM_RD,
  input  IF_ID_BEQ,
  input  IF_ID_BNEQ,
  output forwardA,
  output forwardB
);

  wire comparator_1_eq, comparator_2_eq, comparator_3_eq, comparator_4_eq, not_1_out, not_2_out, or_1_out,
       or_2_out;

  Comparator #(.width(4)) comparator_1 (.a(EX_MEM_RD), .b(4'b0000), .eq(comparator_1_eq));  // open: gt, lt
  Comparator #(.width(4)) comparator_2 (.a(EX_MEM_RD), .b(4'b0000), .eq(comparator_2_eq));  // open: gt, lt
  Comparator #(.width(4)) comparator_3 (.a(IF_ID_RS), .b(EX_MEM_RD), .eq(comparator_3_eq));  // open: gt, lt
  or or_1 (or_1_out, IF_ID_BEQ, IF_ID_BNEQ);
  not not_1 (not_1_out, comparator_1_eq);
  Comparator #(.width(4)) comparator_4 (.a(IF_ID_RT), .b(EX_MEM_RD), .eq(comparator_4_eq));  // open: gt, lt
  or or_2 (or_2_out, IF_ID_BEQ, IF_ID_BNEQ);
  not not_2 (not_2_out, comparator_2_eq);
  and and_1 (forwardA, comparator_3_eq, or_1_out, not_1_out, EX_MEM_REGWRITE);
  and and_2 (forwardB, comparator_4_eq, or_2_out, not_2_out, EX_MEM_REGWRITE);
endmodule

module Branch_L_Forward (
  input  [3:0] IF_ID_RS,
  input  [3:0] IF_ID_RT,
  input  MEM_WB_MEMREAD,
  input  [3:0] MEM_WB_RD,
  input  IF_ID_BEQ,
  input  IF_ID_BNEQ,
  output forwardA,
  output forwardB
);

  wire comparator_1_eq, comparator_2_eq, comparator_3_eq, comparator_4_eq, not_1_out, not_2_out, or_1_out,
       or_2_out;

  Comparator #(.width(4)) comparator_1 (.a(MEM_WB_RD), .b(4'b0000), .eq(comparator_1_eq));  // open: gt, lt
  Comparator #(.width(4)) comparator_2 (.a(MEM_WB_RD), .b(4'b0000), .eq(comparator_2_eq));  // open: gt, lt
  Comparator #(.width(4)) comparator_3 (.a(IF_ID_RS), .b(MEM_WB_RD), .eq(comparator_3_eq));  // open: gt, lt
  or or_1 (or_1_out, IF_ID_BEQ, IF_ID_BNEQ);
  not not_1 (not_1_out, comparator_1_eq);
  Comparator #(.width(4)) comparator_4 (.a(IF_ID_RT), .b(MEM_WB_RD), .eq(comparator_4_eq));  // open: gt, lt
  or or_2 (or_2_out, IF_ID_BEQ, IF_ID_BNEQ);
  not not_2 (not_2_out, comparator_2_eq);
  and and_1 (forwardA, comparator_3_eq, or_1_out, not_1_out, MEM_WB_MEMREAD);
  and and_2 (forwardB, comparator_4_eq, or_2_out, not_2_out, MEM_WB_MEMREAD);
endmodule
